# Fritzing sketch K+Linear (saved by Fritzing 0.9.3b)
breadboards: 8

parts:
  IC1 = L293D [package=THT]
  IC3 = L293D [package=THT]
  U2 = 74HC04_HEX_INVERTER [package=dil14]
  U3 = 74HC595 [package="DIP16 [THT]"]
  IC5 = L293D [package=THT]
  IC6 = L293D [package=THT]
  IC7 = L293D [package=THT]
  IC8 = L293D [package=THT]
  U4 = 74HC04_HEX_INVERTER [package=dil14]
  U5 = 74HC04_HEX_INVERTER [package=dil14]
  U6 = 74HC595 [package="DIP16 [THT]"]
  IC9 = L293D [package=THT]
  IC10 = L293D [package=THT]
  IC11 = L293D [package=THT]
  IC12 = L293D [package=THT]
  U7 = 74HC04_HEX_INVERTER [package=dil14]
  U8 = 74HC04_HEX_INVERTER [package=dil14]
  U9 = 74HC595 [package="DIP16 [THT]"]
  IC13 = L293D [package=THT]
  IC14 = L293D [package=THT]
  IC15 = L293D [package=THT]
  IC16 = L293D [package=THT]
  U10 = 74HC04_HEX_INVERTER [package=dil14]
  U11 = 74HC04_HEX_INVERTER [package=dil14]
  U12 = 74HC595 [package="DIP16 [THT]"]
  U13 = 74HC4051 [package=so16]  # not connected
  U14 = 74HC4051 [package=so16]
  U15 = 74HC4051 [package=so16]
  U16 = 74HC4051 [package=so16]
  LED1 = LED - 5mm [color="Red (633nm)" package="5 mm [THT]"]
  LED2 = LED - 5mm [color="Red (633nm)" package="5 mm [THT]"]
  LED3 = LED - 5mm [color="Red (633nm)" package="5 mm [THT]"]
  LED4 = LED - 5mm [color="Red (633nm)" package="5 mm [THT]"]
  LED6 = LED - 5mm [color="Red (633nm)" package="5 mm [THT]"]
  LED7 = LED - 5mm [color="Red (633nm)" package="5 mm [THT]"]
  LED8 = LED - 5mm [color="Red (633nm)" package="5 mm [THT]"]
  LED9 = LED - 5mm [color="Red (633nm)" package="5 mm [THT]"]
  LED10 = LED - 5mm [color="Red (633nm)" package="5 mm [THT]"]
  LED11 = LED - 5mm [color="Red (633nm)" package="5 mm [THT]"]
  LED12 = LED - 5mm [color="Red (633nm)" package="5 mm [THT]"]
  LED13 = LED - 5mm [color="Red (633nm)" package="5 mm [THT]"]
  S1 = Pushbutton [package="[THT]"]
  S2 = Pushbutton [package="[THT]"]
  R1 = Resistor [tolerance=±5% resistance=150 package=THT]
  R2 = Resistor [tolerance=±5% resistance=150 package=THT]
  R3 = Resistor [tolerance=±5% resistance=150 package=THT]
  R4 = Resistor [tolerance=±5% resistance=150 package=THT]
  R5 = Resistor [tolerance=±5% resistance=150 package=THT]
  R6 = Resistor [tolerance=±5% resistance=150 package=THT]
  R7 = Resistor [tolerance=±5% resistance=150 package=THT]
  R8 = Resistor [tolerance=±5% resistance=150 package=THT]
  R9 = Resistor [tolerance=±5% resistance=150 package=THT]
  R10 = Resistor [tolerance=±5% resistance=150 package=THT]
  R11 = Resistor [tolerance=±5% resistance=150 package=THT]
  R12 = Resistor [tolerance=±5% resistance=150 package=THT]
  R13 = Resistor [tolerance=±5% resistance=150 package=THT]
  LED5 = LED - 5mm [color="Red (633nm)" package="5 mm [THT]"]
  R14 = Slide Potentiometer [maximum_resistance=100kΩ]  # not connected
  M1 = DC Motor  # not connected
  R15 = Slide Potentiometer [maximum_resistance=100kΩ]  # not connected
  M2 = DC Motor  # not connected
  R16 = Slide Potentiometer [maximum_resistance=100kΩ]  # not connected
  R17 = Slide Potentiometer [maximum_resistance=100kΩ]  # not connected
  M3 = DC Motor  # not connected
  M4 = DC Motor  # not connected
  R18 = Slide Potentiometer [maximum_resistance=100kΩ]  # not connected
  R19 = Slide Potentiometer [maximum_resistance=100kΩ]  # not connected
  R20 = Slide Potentiometer [maximum_resistance=100kΩ]  # not connected
  R21 = Slide Potentiometer [maximum_resistance=100kΩ]  # not connected
  M5 = DC Motor  # not connected
  M6 = DC Motor  # not connected
  M7 = DC Motor  # not connected
  M8 = DC Motor  # not connected
  R22 = Slide Potentiometer [maximum_resistance=100kΩ]  # not connected
  R23 = Slide Potentiometer [maximum_resistance=100kΩ]  # not connected
  R24 = Slide Potentiometer [maximum_resistance=100kΩ]  # not connected
  R25 = Slide Potentiometer [maximum_resistance=100kΩ]  # not connected
  R26 = Slide Potentiometer [maximum_resistance=100kΩ]  # not connected
  R27 = Slide Potentiometer [maximum_resistance=100kΩ]  # not connected
  R28 = Slide Potentiometer [maximum_resistance=100kΩ]  # not connected
  R29 = Slide Potentiometer [maximum_resistance=100kΩ]  # not connected
  M9 = DC Motor
  M10 = DC Motor
  M11 = DC Motor
  M12 = DC Motor
  M13 = DC Motor
  M14 = DC Motor
  M15 = DC Motor
  M16 = DC Motor
  R32 = Slide Potentiometer [maximum_resistance=100kΩ]  # not connected
  R33 = Slide Potentiometer [maximum_resistance=100kΩ]  # not connected
  R34 = Slide Potentiometer [maximum_resistance=100kΩ]  # not connected
  R35 = Slide Potentiometer [maximum_resistance=100kΩ]  # not connected
  R36 = Slide Potentiometer [maximum_resistance=100kΩ]  # not connected
  R37 = Slide Potentiometer [maximum_resistance=100kΩ]  # not connected
  R38 = Slide Potentiometer [maximum_resistance=100kΩ]  # not connected
  R39 = Slide Potentiometer [maximum_resistance=100kΩ]  # not connected
  R40 = Slide Potentiometer [maximum_resistance=100kΩ]  # not connected
  R42 = Slide Potentiometer [maximum_resistance=100kΩ]  # not connected
  R44 = Slide Potentiometer [maximum_resistance=100kΩ]  # not connected
  M19 = DC Motor  # not connected
  M20 = DC Motor  # not connected
  M21 = DC Motor  # not connected
  M22 = DC Motor  # not connected
  M23 = DC Motor  # not connected
  M24 = DC Motor  # not connected
  M25 = DC Motor  # not connected
  M29 = DC Motor  # not connected
  M30 = DC Motor  # not connected
  M31 = DC Motor  # not connected
  M32 = DC Motor  # not connected
  D1 = Rectifier Diode [part_number=1N4001 package="300 mil [THT]"]
  S4 = SPST Switch [package=switch-spdt-smd]
  microSD1 = MicroSD Card Module
  Power_plug1 = Power plug
  Composant1 = Arduino Mega 2560 (Rev3)

nets:
  N1: IC1.In_1, U2.1A, U3.Q2
  GND: IC1.0V, IC3.0V, U2.GND, IC5.0V, IC6.0V, IC7.0V, IC8.0V, U4.GND, U5.GND, U6.GND, U6.OE, IC9.0V, IC10.0V, IC11.0V, IC12.0V, U7.GND, U8.GND, U9.GND, U9.OE, IC13.0V, IC14.0V, IC15.0V, IC16.0V, U10.GND, U11.GND, U12.GND, U12.OE, U14.VEE, U14.VSS, U15.VEE, U15.VSS, U16.VEE, U16.VSS, LED1.cathode, LED2.cathode, LED3.cathode, LED4.cathode, LED6.cathode, LED7.cathode, LED8.cathode, LED9.cathode, LED10.cathode, LED11.cathode, LED12.cathode, LED13.cathode, LED5.cathode, D1.cathode, microSD1.GND, Composant1.GND
  N2: IC1.In_2, U2.1Y
  N3: IC1.+Vmotor, IC3.+Vmotor, IC5.+Vmotor, IC6.+Vmotor, IC7.+Vmotor, IC8.+Vmotor, IC9.+Vmotor, IC10.+Vmotor, IC11.+Vmotor, IC12.+Vmotor, IC13.+Vmotor, IC14.+Vmotor, IC15.+Vmotor, IC16.+Vmotor, Power_plug1.VCC
  N4: IC1.In_3, U2.6Y
  N5: IC1.In_4, U2.6A, U3.Q1
  VCC: IC1.+V, IC3.+V, U2.VCC, U3.OE, IC5.+V, IC6.+V, IC7.+V, IC8.+V, U4.VCC, U5.VCC, U6.MR, IC9.+V, IC10.+V, IC11.+V, IC12.+V, U7.VCC, U8.VCC, U9.MR, IC13.+V, IC14.+V, IC15.+V, IC16.+V, U10.VCC, U11.VCC, U12.MR, U14.VDD, U15.VDD, U16.VDD, S1.Pin_1, S1.Pin_2, S2.Pin_1, S2.Pin_2, Composant1.D8_PWM, Composant1.D7_PWM
  N6: IC3.In_1, U2.3Y
  N7: IC3.In_2, U2.3A, U3.Q3
  N8: IC3.In_3, U2.4Y
  N9: IC3.In_4, U2.4A, U3.Q0
  N10: U3.SH_CP, U6.SH_CP, U9.SH_CP, U12.SH_CP, Composant1.D0_RX0
  N11: U3.ST_CP, U6.Q7'
  N12: IC5.In_1, U5.3A, U6.Q5
  N13: IC5.In_2, U5.3Y
  N14: IC5.In_3, U5.4Y
  N15: IC5.In_4, U5.4A, U6.Q7
  N16: IC6.In_1, U4.1A, U6.Q2
  N17: IC6.In_2, U4.1Y
  N18: IC6.In_3, U4.6Y
  N19: IC6.In_4, U4.6A, U6.Q1
  N20: IC7.In_1, U5.1A, U6.Q4
  N21: IC7.In_2, U5.1Y
  N22: IC7.In_3, U5.6Y
  N23: IC7.In_4, U5.6A, U6.Q6
  N24: IC8.In_1, U4.3Y
  N25: IC8.In_2, U4.3A, U6.Q3
  N26: IC8.In_3, U4.4Y
  N27: IC8.In_4, U4.4A, U6.Q0
  N28: U6.ST_CP, U12.ST_CP, Composant1.D1_TX0
  N29: U6.DS, Composant1.D3_PWM
  N30: IC9.In_1, U7.3A, U9.Q5
  N31: IC9.In_2, U7.3Y
  N32: IC9.In_3, U7.4Y
  N33: IC9.In_4, U7.4A, U9.Q7
  N34: IC10.In_1, U8.3Y
  N35: IC10.In_2, U8.3A, U9.Q3
  N36: IC10.In_3, U8.4Y
  N37: IC10.In_4, U8.4A, U9.Q0
  N38: IC11.In_1, U8.1A, U9.Q2
  N39: IC11.In_2, U8.1Y
  N40: IC11.In_3, U8.6Y
  N41: IC11.In_4, U8.6A, U9.Q1
  N42: IC12.In_1, U7.1A, U9.Q4
  N43: IC12.In_2, U7.1Y
  N44: IC12.In_3, U7.6Y
  N45: IC12.In_4, U7.6A, U9.Q6
  N46: U9.ST_CP, U12.Q7'
  N47: IC13.In_1, U10.3A, U12.Q5
  N48: IC13.Out_1_(_Controlled_by_Enable_1_), M11.pin_2
  N49: IC13.In_2, U10.3Y
  N50: IC13.In_3, U10.4Y
  N51: IC13.Out_3_(_Controlled_by_Enable_2_), M16.pin_2
  N52: IC13.In_4, U10.4A, U12.Q7
  N53: IC14.In_1, U11.3Y
  N54: IC14.Out_1_(_Controlled_by_Enable_1_), M12.pin_2
  N55: IC14.In_2, U11.3A, U12.Q3
  N56: IC14.In_3, U11.4Y
  N57: IC14.Out_3_(_Controlled_by_Enable_2_), M10.pin_2
  N58: IC14.In_4, U11.4A, U12.Q0
  N59: IC15.In_1, U11.1A, U12.Q2
  N60: IC15.Out_1_(_Controlled_by_Enable_1_), M14.pin_2
  N61: IC15.In_2, U11.1Y
  N62: IC15.In_3, U11.6Y
  N63: IC15.Out_3_(_Controlled_by_Enable_2_), M13.pin_2
  N64: IC15.In_4, U11.6A, U12.Q1
  N65: IC16.In_1, U10.1A, U12.Q4
  N66: IC16.Out_1_(_Controlled_by_Enable_1_), M15.pin_2
  N67: IC16.In_2, U10.1Y
  N68: IC16.In_3, U10.6Y
  N69: IC16.Out_3_(_Controlled_by_Enable_2_), M9.pin_2
  N70: IC16.In_4, U10.6A, U12.Q6
  N71: U12.DS, Composant1.D2_PWM
  N72: LED1.anode, R3.Pin_0
  N73: LED2.anode, R5.Pin_0
  N74: LED3.anode, R8.Pin_0
  N75: LED4.anode, R10.Pin_0
  N76: LED6.anode, R1.Pin_1
  N77: LED7.anode, R2.Pin_1
  N78: LED8.anode, R4.Pin_1
  N79: LED9.anode, R6.Pin_1
  N80: LED10.anode, R7.Pin_1
  N81: LED11.anode, R9.Pin_1
  N82: LED12.anode, R11.Pin_1
  N83: LED13.anode, R12.Pin_1
  N84: S1.Pin_3, S1.Pin_4
  N85: S2.Pin_3, S2.Pin_4
  N86: R1.Pin_0, Composant1.D14/TX3
  N87: R2.Pin_0, Composant1.D15/RX3
  N88: R3.Pin_1, Composant1.D9_PWM
  N89: R4.Pin_0, Composant1.D16_PWM/TX2
  N90: R5.Pin_1, Composant1.D10_PWM
  N91: R6.Pin_0, Composant1.D17_PWM/RX2
  N92: R7.Pin_0, Composant1.D18/TX1
  N93: R8.Pin_1, Composant1.D11_PWM
  N94: R9.Pin_0, Composant1.D19/RX1
  N95: R10.Pin_1, Composant1.D12_PWM
  N96: R11.Pin_0, Composant1.D20/SDA
  N97: R12.Pin_0, Composant1.D21/SCL
  N98: R13.Pin_0, LED5.anode
  N99: R13.Pin_1, Composant1.D13_PWM
  N100: D1.anode, S4.P
  N101: S4.S, Composant1.D23
  VCC_2: microSD1.VCC, Composant1.3V3
